// Logisim project Pipeline.circ as structural Verilog: 11 circuits, main circuit main
module main (
  input  [2:0] in_1,
  input  [15:0] in_2,
  input  [15:0] in_3,
  output [15:0] out_4
);

  wire [15:0] adder_1_out, and_1_out, not_1_out, or_1_out, shifter_1_out, shifter_2_out, subtractor_1_out,
       xor_1_out;

  Adder #(.width(16)) adder_1 (.a(in_2), .b(in_3), .out(adder_1_out));  // open: cin, cout
  Subtractor #(.width(16)) subtractor_1 (.a(in_2), .b(in_3), .out(subtractor_1_out));  // open: bin, bout
  assign or_1_out = in_2 | in_3;  // OR_Gate or_1, 16 bits wide
  assign and_1_out = in_2 & in_3;  // AND_Gate and_1, 16 bits wide
  assign not_1_out = ~in_3;  // NOT_Gate not_1, 16 bits wide
  assign xor_1_out = in_2 ^ in_3;  // XOR_Gate xor_1, 16 bits wide
  Shifter #(.width(16)) shifter_1 (.in(in_2), .\dist (in_3[3:0]), .out(shifter_1_out));
  Shifter #(.shift("lr"), .width(16)) shifter_2 (.in(in_2), .\dist (in_3[3:0]), .out(shifter_2_out));
  Multiplexer #(.select(3), .width(16)) multiplexer_1 (
    .in0(adder_1_out), .in1(subtractor_1_out), .in2(or_1_out), .in3(and_1_out), .in4(not_1_out),
    .in5(xor_1_out), .in6(shifter_1_out), .in7(shifter_2_out), .out(out_4), .sel(in_1));
endmodule

module RegisterFile (
  input  WRITE_EN,
  input  [2:0] RD,
  input  [2:0] RS,
  input  [15:0] WRITE_DATA,
  input  in_5,
  input  [2:0] REG_WRITE,
  output [15:0] A_OUT,
  output [15:0] B_OUT
);

  wire demultiplexer_1_out0, demultiplexer_1_out1, demultiplexer_1_out2, demultiplexer_1_out3,
       demultiplexer_1_out4, demultiplexer_1_out5, demultiplexer_1_out6, demultiplexer_1_out7;
  wire [15:0] register_1_q, register_2_q, register_3_q, register_4_q, register_5_q, register_6_q,
       register_7_q, register_8_q;

  Demultiplexer #(.select(3)) demultiplexer_1 (
    .out0(demultiplexer_1_out0), .out1(demultiplexer_1_out1), .out2(demultiplexer_1_out2),
    .out3(demultiplexer_1_out3), .out4(demultiplexer_1_out4), .out5(demultiplexer_1_out5),
    .out6(demultiplexer_1_out6), .out7(demultiplexer_1_out7), .in(WRITE_EN), .sel(REG_WRITE));
  Register #(.width(16)) register_1 (
    .D(WRITE_DATA), .en(demultiplexer_1_out0), .clk(in_5), .Q(register_1_q));  // open: clr
  Register #(.width(16)) register_2 (
    .D(WRITE_DATA), .en(demultiplexer_1_out1), .clk(in_5), .Q(register_2_q));  // open: clr
  Register #(.width(16)) register_3 (
    .D(WRITE_DATA), .en(demultiplexer_1_out2), .clk(in_5), .Q(register_3_q));  // open: clr
  Register #(.width(16)) register_4 (
    .D(WRITE_DATA), .en(demultiplexer_1_out3), .clk(in_5), .Q(register_4_q));  // open: clr
  Register #(.width(16)) register_5 (
    .D(WRITE_DATA), .en(demultiplexer_1_out4), .clk(in_5), .Q(register_5_q));  // open: clr
  Register #(.width(16)) register_6 (
    .D(WRITE_DATA), .en(demultiplexer_1_out5), .clk(in_5), .Q(register_6_q));  // open: clr
  Register #(.width(16)) register_7 (
    .D(WRITE_DATA), .en(demultiplexer_1_out6), .clk(in_5), .Q(register_7_q));  // open: clr
  Register #(.width(16)) register_8 (
    .D(WRITE_DATA), .en(demultiplexer_1_out7), .clk(in_5), .Q(register_8_q));  // open: clr
  Multiplexer #(.select(3), .width(16)) multiplexer_1 (
    .in0(register_1_q), .in1(register_2_q), .in2(register_3_q), .in3(register_4_q), .in4(register_5_q),
    .in5(register_6_q), .in6(register_7_q), .in7(register_8_q), .out(B_OUT), .sel(RS));
  Multiplexer #(.select(3), .width(16)) multiplexer_2 (
    .in0(register_1_q), .in1(register_2_q), .in2(register_3_q), .in3(register_4_q), .in4(register_5_q),
    .in5(register_6_q), .in6(register_7_q), .in7(register_8_q), .out(A_OUT), .sel(RD));
endmodule

module CPU (
);

  wire clock_1_out, clock_2_out, controller_1_jmp, controller_1_mem_write, controller_1_r_i,
       controller_1_reg_write, controller_1_sign_ext, is_zero_1_out_2, is_zero_2_out_2;
  wire [1:0] controller_1_jmp_mode, controller_1_written;
  wire [2:0] controller_1_alu_func, controller_1_reg_d, controller_1_reg_s;
  wire [7:0] controller_1_imm8;
  wire [15:0] adder_1_out, bit_extender_1_out, bit_extender_2_out, counter_1_q, main_1_out_4,
       multiplexer_1_out, multiplexer_2_out, multiplexer_3_out, multiplexer_4_out, multiplexer_5_out,
       multiplexer_6_out, multiplexer_7_out, multiplexer_8_out, ram_1_dout, registerfile_1_a_out,
       registerfile_1_b_out, rom_1_data;

  Adder #(.width(16)) adder_1 (.a(16'h1), .b(counter_1_q), .out(adder_1_out));  // open: cin, cout
  IS_ZERO is_zero_1 (.in_1(registerfile_1_a_out), .out_2(is_zero_1_out_2));
  Counter #(.max('hffff), .width(16)) counter_1 (
    .load(1'b1), .D(multiplexer_1_out), .Q(counter_1_q), .clk(clock_1_out));  // open: count, carry, up, clr
  Multiplexer #(.width(16)) multiplexer_1 (
    .in0(adder_1_out), .in1(multiplexer_2_out), .out(multiplexer_1_out), .sel(controller_1_jmp));
  Multiplexer #(.select(2), .width(16)) multiplexer_2 (
    .in0(multiplexer_6_out), .in1(multiplexer_3_out), .in2(multiplexer_4_out), .in3(counter_1_q),
    .out(multiplexer_2_out), .sel(controller_1_jmp_mode));
  ROM #(.addrWidth(16), .dataWidth(16)) rom_1 (.addr(counter_1_q), .data(rom_1_data));
  Multiplexer #(.width(16)) multiplexer_3 (
    .in0(adder_1_out), .in1(multiplexer_6_out), .out(multiplexer_3_out), .sel(is_zero_1_out_2));
  Multiplexer #(.width(16)) multiplexer_4 (
    .in0(multiplexer_6_out), .in1(adder_1_out), .out(multiplexer_4_out), .sel(is_zero_2_out_2));
  IS_ZERO is_zero_2 (.in_1(registerfile_1_a_out), .out_2(is_zero_2_out_2));
  Clock clock_1 (.out(clock_1_out));
  assign bit_extender_1_out = {{8{1'b0}}, controller_1_imm8};  // Bit_Extender bit_extender_1
  assign bit_extender_2_out = {{8{controller_1_imm8[7]}}, controller_1_imm8};  // Bit_Extender bit_extender_2
  RegisterFile registerfile_1 (
    .RS(controller_1_reg_s), .WRITE_DATA(multiplexer_8_out), .WRITE_EN(controller_1_reg_write),
    .in_5(clock_1_out), .RD(controller_1_reg_d), .A_OUT(registerfile_1_a_out), .B_OUT(registerfile_1_b_out));  // open: REG_WRITE
  Multiplexer #(.width(16)) multiplexer_5 (
    .in0(bit_extender_1_out), .in1(bit_extender_2_out), .out(multiplexer_5_out), .sel(controller_1_sign_ext));
  Multiplexer #(.width(16)) multiplexer_6 (
    .in0(registerfile_1_b_out), .in1(bit_extender_1_out), .out(multiplexer_6_out), .sel(controller_1_r_i));
  Controller controller_1 (
    .in_1(rom_1_data), .IMM8(controller_1_imm8), .REG_S(controller_1_reg_s),
    .SIGN_EXT(controller_1_sign_ext), .R_I(controller_1_r_i), .REG_D(controller_1_reg_d),
    .ALU_FUNC(controller_1_alu_func), .REG_WRITE(controller_1_reg_write), .MEM_WRITE(controller_1_mem_write),
    .JMP_MODE(controller_1_jmp_mode), .JMP(controller_1_jmp), .Written(controller_1_written));
  Multiplexer #(.width(16)) multiplexer_7 (
    .in0(registerfile_1_b_out), .in1(multiplexer_5_out), .out(multiplexer_7_out), .sel(controller_1_r_i));
  Multiplexer #(.select(2), .width(16)) multiplexer_8 (
    .in0(registerfile_1_b_out), .in1(multiplexer_5_out), .in2(ram_1_dout), .in3(main_1_out_4),
    .out(multiplexer_8_out), .sel(controller_1_written));
  main main_1 (
    .in_2(registerfile_1_a_out), .in_3(multiplexer_7_out), .in_1(controller_1_alu_func), .out_4(main_1_out_4));
  RAM #(.addrWidth(16), .asyncread("true"), .dataWidth(16)) ram_1 (
    .addr(multiplexer_7_out), .we(controller_1_mem_write), .oe(1'b1), .clk(clock_2_out),
    .din(registerfile_1_a_out), .dout(ram_1_dout));
  Clock clock_2 (.out(clock_2_out));

  // Notes on the sheet:
  //   contents of rom_1 (hex, n*v repeats v):
  //   1805 190a d707 2007 8f01 2107 8f01 1a0a 2207 480b 7000 8f01 2307 1307 9b03 3003 8b01 3103 8b02 5823
  //   9801 8f01 2007 8f01 2107 8f01 1a1d 2207 480b 8801 1703 3307 9f01 3207 4002 1001 481e
endmodule

module Controller (
  input  [15:0] in_1,
  output [7:0] IMM8,
  output [2:0] REG_S,
  output SIGN_EXT,
  output R_I,
  output [2:0] REG_D,
  output [2:0] ALU_FUNC,
  output REG_WRITE,
  output MEM_WRITE,
  output [1:0] JMP_MODE,
  output JMP,
  output [1:0] Written
);

  wire and_1_out, nor_1_out, not_1_out, not_2_out, not_3_out, or_2_out, or_3_out, xor_1_out;

  or or_1 (Written[1], in_1[13], in_1[15]);
  Multiplexer multiplexer_1 (.in0(in_1[11]), .in1(in_1[15]), .out(Written[0]), .sel(Written[1]));
  and and_1 (and_1_out, Written[1], xor_1_out);
  or or_2 (or_2_out, and_1_out, MEM_WRITE);
  xor xor_1 (xor_1_out, Written[1], Written[0]);
  not not_1 (not_1_out, or_2_out);
  not not_2 (not_2_out, in_1[15]);
  or or_3 (or_3_out, in_1[15], in_1[12]);
  and and_2 (JMP, in_1[14], not_2_out);
  and and_3 (SIGN_EXT, in_1[7], not_1_out);
  nor nor_1 (nor_1_out, in_1[12], in_1[15], JMP);
  not not_3 (not_3_out, JMP);
  and and_4 (REG_WRITE, or_3_out, not_3_out);
  and and_5 (MEM_WRITE, nor_1_out, in_1[13]);

  assign ALU_FUNC = in_1[14:12];
  assign IMM8 = in_1[7:0];
  assign JMP_MODE = in_1[13:12];
  assign R_I = in_1[11];
  assign REG_D = in_1[10:8];
  assign REG_S = in_1[2:0];
endmodule

module IS_ZERO (
  input  [15:0] in_1,
  output out_2
);

  wire or_1_out, or_2_out, or_3_out, or_4_out, or_5_out, or_6_out, or_7_out, or_8_out, or_9_out, or_10_out,
       or_11_out, or_12_out, or_13_out, or_14_out, or_15_out;

  or or_1 (or_1_out, in_1[0], in_1[1]);
  or or_2 (or_2_out, in_1[2], in_1[3]);
  or or_3 (or_3_out, in_1[14], in_1[15]);
  or or_4 (or_4_out, in_1[12], in_1[13]);
  or or_5 (or_5_out, in_1[4], in_1[5]);
  or or_6 (or_6_out, in_1[8], in_1[9]);
  or or_7 (or_7_out, in_1[10], in_1[11]);
  or or_8 (or_8_out, in_1[6], in_1[7]);
  or or_9 (or_9_out, or_1_out, or_2_out);
  or or_10 (or_10_out, or_5_out, or_8_out);
  or or_11 (or_11_out, or_6_out, or_7_out);
  or or_12 (or_12_out, or_4_out, or_3_out);
  or or_13 (or_13_out, or_11_out, or_12_out);
  or or_14 (or_14_out, or_9_out, or_10_out);
  or or_15 (or_15_out, or_14_out, or_13_out);
  not not_1 (out_2, or_15_out);
endmodule

module Pipeline (
  input  in_1
);

  wire clock_1_out, controller_1_jmp, controller_1_mem_write, controller_1_r_i, controller_1_reg_write,
       controller_1_sign_ext, decode_register_1_ext, decode_register_1_jump, decode_register_1_mw,
       decode_register_1_r_or_i, decode_register_1_rw, exe_register_1_m_w, exe_register_1_r_w,
       mem_register_1_m_w, mem_register_1_r_w, write_register_1_write_reg;
  wire [1:0] controller_1_jmp_mode, controller_1_written, decode_register_1_w_controll,
       exe_register_1_write_mode, mem_register_1_w_controll, write_register_1_w_controll;
  wire [2:0] controller_1_alu_func, controller_1_reg_d, controller_1_reg_s, decode_register_1_alu,
       decode_register_1_regd_out, decode_register_1_regs_out, exe_register_1_alu, exe_register_1_rd,
       mem_register_1_rd, write_register_1_reg_dest;
  wire [7:0] controller_1_imm8, decode_register_1_imm_out;
  wire [15:0] adder_1_out, bit_extender_1_out, bit_extender_2_out, exe_register_1_rd_out,
       exe_register_1_rs_out, forward_dest_1_val, main_1_out_4, mem_register_1_addr, mem_register_1_alu_r,
       mem_register_1_data, multiplexer_1_out, multiplexer_2_out, multiplexer_3_out, ram_1_dout,
       register_1_q, registerfile_1_a_out, registerfile_1_b_out, rom_1_data, write_register_1_alu_res,
       write_register_1_memory_res, write_register_1_rs_out;

  Register #(.width(16)) register_1 (.D(adder_1_out), .Q(register_1_q), .clk(clock_1_out));  // open: en, clr
  Adder #(.width(16)) adder_1 (.a(register_1_q), .b(16'h1), .out(adder_1_out));  // open: cin, cout
  ROM #(.addrWidth(16), .dataWidth(16)) rom_1 (.addr(register_1_q), .data(rom_1_data));
  Clock clock_1 (.out(clock_1_out));
  Controller controller_1 (
    .in_1(rom_1_data), .IMM8(controller_1_imm8), .REG_S(controller_1_reg_s),
    .SIGN_EXT(controller_1_sign_ext), .R_I(controller_1_r_i), .REG_D(controller_1_reg_d),
    .ALU_FUNC(controller_1_alu_func), .REG_WRITE(controller_1_reg_write), .MEM_WRITE(controller_1_mem_write),
    .JMP_MODE(controller_1_jmp_mode), .JMP(controller_1_jmp), .Written(controller_1_written));
  Decode_register decode_register_1 (
    .IMM_8(controller_1_imm8), .REG_S(controller_1_reg_s), .SIGN_EXT(controller_1_sign_ext),
    .R_I(controller_1_r_i), .REG_D(controller_1_reg_d), .ALU_FUNC(controller_1_alu_func),
    .REG_WRITE(controller_1_reg_write), .MEM_WRITE(controller_1_mem_write), .JMP_MODE(controller_1_jmp_mode),
    .JMP(controller_1_jmp), .WRITTEN(controller_1_written), .CLK(clock_1_out), .in_13(in_1),
    .IMM_OUT(decode_register_1_imm_out), .REGS_OUT(decode_register_1_regs_out), .EXT(decode_register_1_ext),
    .R_OR_I(decode_register_1_r_or_i), .REGD_OUT(decode_register_1_regd_out), .ALU(decode_register_1_alu),
    .RW(decode_register_1_rw), .MW(decode_register_1_mw), .JUMP(decode_register_1_jump),
    .W_CONTROLL(decode_register_1_w_controll));  // open: MODE_JMP
  RegisterFile registerfile_1 (
    .RS(decode_register_1_regs_out), .WRITE_DATA(multiplexer_3_out), .WRITE_EN(write_register_1_write_reg),
    .REG_WRITE(write_register_1_reg_dest), .in_5(clock_1_out), .RD(decode_register_1_regd_out),
    .A_OUT(registerfile_1_a_out), .B_OUT(registerfile_1_b_out));
  assign bit_extender_1_out = {{8{1'b0}}, decode_register_1_imm_out};  // Bit_Extender bit_extender_1
  assign bit_extender_2_out = {{8{decode_register_1_imm_out[7]}}, decode_register_1_imm_out};  // Bit_Extender bit_extender_2
  Multiplexer #(.width(16)) multiplexer_1 (
    .in0(bit_extender_1_out), .in1(bit_extender_2_out), .out(multiplexer_1_out), .sel(decode_register_1_ext));
  FORWARD_DEST forward_dest_1 (
    .DECODE_REG(decode_register_1_regd_out), .DECODE_VAL(registerfile_1_a_out),
    .EXECUTE_REG(exe_register_1_rd), .EXECUTE_RW(exe_register_1_r_w),
    .EXECUTE_WRITTEN(exe_register_1_write_mode), .EXECUTE_ALU(main_1_out_4),
    .EXECUTE_RS_IMM8(exe_register_1_rs_out), .VAL(forward_dest_1_val));  // open: MEMORY_REG, MEMORY_ALU, WRITE_ALU, WRITE_REG
  Multiplexer #(.width(16)) multiplexer_2 (
    .in0(registerfile_1_b_out), .in1(multiplexer_1_out), .out(multiplexer_2_out),
    .sel(decode_register_1_r_or_i));
  Exe_register exe_register_1 (
    .ALU_FUNC(decode_register_1_alu), .REG_S(decode_register_1_regs_out), .REG_D(decode_register_1_regd_out),
    .RD_VAL(forward_dest_1_val), .RS_VAL(multiplexer_2_out), .WRITTEN(decode_register_1_w_controll),
    .REG_WRITE(decode_register_1_rw), .MEM_WRITE(decode_register_1_mw), .R_I(decode_register_1_ext),
    .JMP(decode_register_1_jump), .CLK(clock_1_out), .in_12(in_1), .ALU(exe_register_1_alu),
    .RD(exe_register_1_rd), .RD_OUT(exe_register_1_rd_out), .RS_OUT(exe_register_1_rs_out),
    .WRITE_MODE(exe_register_1_write_mode), .R_W(exe_register_1_r_w), .M_W(exe_register_1_m_w));  // open: RS, R_OR_I, JUMP
  main main_1 (
    .in_2(exe_register_1_rd_out), .in_3(exe_register_1_rs_out), .in_1(exe_register_1_alu),
    .out_4(main_1_out_4));
  Mem_register mem_register_1 (
    .RD_OUT(exe_register_1_rd_out), .MEM_WRITE(exe_register_1_m_w), .REG_WRITE(exe_register_1_r_w),
    .RS_OUT(exe_register_1_rs_out), .REG_D(exe_register_1_rd), .WRITTEN(exe_register_1_write_mode),
    .ALU(main_1_out_4), .CLK(clock_1_out), .in_9(in_1), .DATA(mem_register_1_data), .M_W(mem_register_1_m_w),
    .R_W(mem_register_1_r_w), .ADDR(mem_register_1_addr), .RD(mem_register_1_rd),
    .W_CONTROLL(mem_register_1_w_controll), .ALU_R(mem_register_1_alu_r));
  RAM #(.addrWidth(16), .asyncread("true"), .dataWidth(16)) ram_1 (
    .addr(mem_register_1_addr), .we(mem_register_1_m_w), .oe(1'b1), .clk(clock_1_out),
    .din(mem_register_1_data), .dout(ram_1_dout));
  Multiplexer #(.select(2), .width(16)) multiplexer_3 (
    .in0(write_register_1_rs_out), .in1(write_register_1_rs_out), .in2(write_register_1_memory_res),
    .in3(write_register_1_alu_res), .out(multiplexer_3_out), .sel(write_register_1_w_controll));
  Write_register write_register_1 (
    .RD(mem_register_1_rd), .ALU_OP(mem_register_1_alu_r), .RS_VAL(mem_register_1_addr),
    .MEM_VAL(ram_1_dout), .WRITTEN(mem_register_1_w_controll), .W_REG(mem_register_1_r_w), .CLK(clock_1_out),
    .in_8(in_1), .REG_DEST(write_register_1_reg_dest), .ALU_RES(write_register_1_alu_res),
    .RS_OUT(write_register_1_rs_out), .MEMORY_RES(write_register_1_memory_res),
    .W_CONTROLL(write_register_1_w_controll), .WRITE_REG(write_register_1_write_reg));

  // Notes on the sheet:
  //   contents of rom_1 (hex, n*v repeats v):
  //   1802 8802 880a
endmodule

module Decode_register (
  input  [7:0] IMM_8,
  input  [2:0] REG_S,
  input  SIGN_EXT,
  input  R_I,
  input  [2:0] REG_D,
  input  [2:0] ALU_FUNC,
  input  REG_WRITE,
  input  MEM_WRITE,
  input  [1:0] JMP_MODE,
  input  JMP,
  input  [1:0] WRITTEN,
  input  CLK,
  input  in_13,
  output [7:0] IMM_OUT,
  output [2:0] REGS_OUT,
  output EXT,
  output R_OR_I,
  output [2:0] REGD_OUT,
  output [2:0] ALU,
  output RW,
  output MW,
  output [1:0] MODE_JMP,
  output JUMP,
  output [1:0] W_CONTROLL
);

  Register register_1 (.D(IMM_8), .en(in_13), .Q(IMM_OUT), .clk(CLK));  // open: clr
  Register #(.width(3)) register_2 (.D(REG_S), .en(in_13), .Q(REGS_OUT), .clk(CLK));  // open: clr
  Register #(.width(1)) register_3 (.D(SIGN_EXT), .en(in_13), .Q(EXT), .clk(CLK));  // open: clr
  Register #(.width(1)) register_4 (.D(R_I), .en(in_13), .Q(R_OR_I), .clk(CLK));  // open: clr
  Register #(.width(3)) register_5 (.D(REG_D), .en(in_13), .Q(REGD_OUT), .clk(CLK));  // open: clr
  Register #(.width(3)) register_6 (.D(ALU_FUNC), .en(in_13), .Q(ALU), .clk(CLK));  // open: clr
  Register #(.width(1)) register_7 (.D(REG_WRITE), .en(in_13), .Q(RW), .clk(CLK));  // open: clr
  Register #(.width(1)) register_8 (.D(MEM_WRITE), .en(in_13), .Q(MW), .clk(CLK));  // open: clr
  Register #(.width(2)) register_9 (.D(JMP_MODE), .en(in_13), .Q(MODE_JMP), .clk(CLK));  // open: clr
  Register #(.width(1)) register_10 (.D(JMP), .en(in_13), .Q(JUMP), .clk(CLK));  // open: clr
  Register #(.width(2)) register_11 (.D(WRITTEN), .en(in_13), .Q(W_CONTROLL), .clk(CLK));  // open: clr
endmodule

module Exe_register (
  input  [2:0] ALU_FUNC,
  input  [2:0] REG_S,
  input  [2:0] REG_D,
  input  [15:0] RD_VAL,
  input  [15:0] RS_VAL,
  input  [1:0] WRITTEN,
  input  REG_WRITE,
  input  MEM_WRITE,
  input  R_I,
  input  JMP,
  input  CLK,
  input  in_12,
  output [2:0] ALU,
  output [2:0] RS,
  output [2:0] RD,
  output [15:0] RD_OUT,
  output [15:0] RS_OUT,
  output [1:0] WRITE_MODE,
  output R_W,
  output M_W,
  output R_OR_I,
  output JUMP
);

  Register #(.width(3)) register_1 (.D(ALU_FUNC), .en(in_12), .Q(ALU), .clk(CLK));  // open: clr
  Register #(.width(3)) register_2 (.D(REG_S), .en(in_12), .Q(RS), .clk(CLK));  // open: clr
  Register #(.width(3)) register_3 (.D(REG_D), .en(in_12), .Q(RD), .clk(CLK));  // open: clr
  Register #(.width(16)) register_4 (.D(RD_VAL), .en(in_12), .Q(RD_OUT), .clk(CLK));  // open: clr
  Register #(.width(16)) register_5 (.D(RS_VAL), .en(in_12), .Q(RS_OUT), .clk(CLK));  // open: clr
  Register #(.width(2)) register_6 (.D(WRITTEN), .en(in_12), .Q(WRITE_MODE), .clk(CLK));  // open: clr
  Register #(.width(1)) register_7 (.D(REG_WRITE), .en(in_12), .Q(R_W), .clk(CLK));  // open: clr
  Register #(.width(1)) register_8 (.D(MEM_WRITE), .en(in_12), .Q(M_W), .clk(CLK));  // open: clr
  Register #(.width(1)) register_9 (.D(R_I), .en(in_12), .Q(R_OR_I), .clk(CLK));  // open: clr
  Register #(.width(1)) register_10 (.D(JMP), .en(in_12), .Q(JUMP), .clk(CLK));  // open: clr
endmodule

module Mem_register (
  input  [15:0] RD_OUT,
  input  MEM_WRITE,
  input  REG_WRITE,
  input  [15:0] RS_OUT,
  input  [2:0] REG_D,
  input  [1:0] WRITTEN,
  input  [15:0] ALU,
  input  CLK,
  input  in_9,
  output [15:0] DATA,
  output M_W,
  output R_W,
  output [15:0] ADDR,
  output [2:0] RD,
  output [1:0] W_CONTROLL,
  output [15:0] ALU_R
);

  Register #(.width(16)) register_1 (.D(RD_OUT), .en(in_9), .Q(DATA), .clk(CLK));  // open: clr
  Register #(.width(1)) register_2 (.D(MEM_WRITE), .en(in_9), .Q(M_W), .clk(CLK));  // open: clr
  Register #(.width(1)) register_3 (.D(REG_WRITE), .en(in_9), .Q(R_W), .clk(CLK));  // open: clr
  Register #(.width(16)) register_4 (.D(RS_OUT), .en(in_9), .Q(ADDR), .clk(CLK));  // open: clr
  Register #(.width(3)) register_5 (.D(REG_D), .en(in_9), .Q(RD), .clk(CLK));  // open: clr
  Register #(.width(2)) register_6 (.D(WRITTEN), .en(in_9), .Q(W_CONTROLL), .clk(CLK));  // open: clr
  Register #(.width(16)) register_7 (.D(ALU), .en(in_9), .Q(ALU_R), .clk(CLK));  // open: clr
endmodule

module Write_register (
  input  [2:0] RD,
  input  [15:0] ALU_OP,
  input  [15:0] RS_VAL,
  input  [15:0] MEM_VAL,
  input  [1:0] WRITTEN,
  input  W_REG,
  input  CLK,
  input  in_8,
  output [2:0] REG_DEST,
  output [15:0] ALU_RES,
  output [15:0] RS_OUT,
  output [15:0] MEMORY_RES,
  output [1:0] W_CONTROLL,
  output WRITE_REG
);

  Register #(.width(3)) register_1 (.D(RD), .en(in_8), .Q(REG_DEST), .clk(CLK));  // open: clr
  Register #(.width(16)) register_2 (.D(ALU_OP), .en(in_8), .Q(ALU_RES), .clk(CLK));  // open: clr
  Register #(.width(16)) register_3 (.D(RS_VAL), .en(in_8), .Q(RS_OUT), .clk(CLK));  // open: clr
  Register #(.width(16)) register_4 (.D(MEM_VAL), .en(in_8), .Q(MEMORY_RES), .clk(CLK));  // open: clr
  Register #(.width(2)) register_5 (.D(WRITTEN), .en(in_8), .Q(W_CONTROLL), .clk(CLK));  // open: clr
  Register #(.width(1)) register_6 (.D(W_REG), .en(in_8), .Q(WRITE_REG), .clk(CLK));  // open: clr
endmodule

module FORWARD_DEST (
  input  [2:0] DECODE_REG,
  input  [15:0] DECODE_VAL,
  input  [2:0] EXECUTE_REG,
  input  EXECUTE_RW,
  input  [1:0] EXECUTE_WRITTEN,
  input  [15:0] EXECUTE_ALU,
  input  [15:0] EXECUTE_RS_IMM8,
  input  [2:0] MEMORY_REG,
  input  [15:0] MEMORY_ALU,
  input  [15:0] WRITE_ALU,
  input  [2:0] WRITE_REG,
  output [15:0] VAL
);

  wire and_1_out, not_1_out, or_1_out, or_2_out;
  wire [2:0] xor_1_out;
  wire [15:0] multiplexer_1_out, multiplexer_2_out;

  Multiplexer #(.width(16)) multiplexer_1 (
    .in0(EXECUTE_RS_IMM8), .in1(EXECUTE_ALU), .out(multiplexer_1_out), .sel(and_1_out));
  and and_1 (and_1_out, EXECUTE_WRITTEN[0], EXECUTE_WRITTEN[1]);
  Multiplexer #(.width(16)) multiplexer_2 (
    .in0(DECODE_VAL), .in1(multiplexer_1_out), .out(multiplexer_2_out), .sel(EXECUTE_RW));
  assign xor_1_out = DECODE_REG ^ EXECUTE_REG;  // XOR_Gate xor_1, 3 bits wide
  or or_1 (or_1_out, xor_1_out[0], xor_1_out[1]);
  Multiplexer #(.width(16)) multiplexer_3 (.in0(DECODE_VAL), .in1(multiplexer_2_out), .out(VAL), .sel(not_1_out));
  not not_1 (not_1_out, or_2_out);
  or or_2 (or_2_out, or_1_out, xor_1_out[2]);
endmodule
